# Fritzing sketch coche (saved by Fritzing 0.9.3b)
breadboards: 1

parts:
  Componente1 = Arduino Uno (Rev3)
  R1 = Resistor [tolerance=±5% resistance=220 package=THT]
  JP1 = Header 6 [package=1x06-smd]  # not connected
  S1 = Pushbutton [package="[THT]"]
  R2 = Resistor [tolerance=±5% resistance=10k package=THT]
  LED1 = LED - 5mm [color="Red (633nm)" package="5 mm [THT]"]

nets:
  N1: Componente1.GND, R2.Pin_0, LED1.cathode
  N2: R1.Pin_1, LED1.anode
  N3: S1.Pin_1, S1.Pin_2, R2.Pin_1
  N4: S1.Pin_3, S1.Pin_4
